// Logisim project Projet.circ as structural Verilog: 8 circuits, main circuit main
module main (
  input  S3,
  input  S2,
  input  S1,
  input  S0,
  input  S1_2,
  input  S0_2,
  input  In_0,
  input  In_1,
  input  In_2,
  input  In_3,
  input  S3_2,
  input  S2_2,
  input  S1_3,
  input  S0_3
);

  wire button_1_out, button_2_out, demux_1_s0, demux_2_s0, demux_3_s0, demux_4_s0, or_1_out, or_2_out,
       or_3_out, or_4_out;
  wire [3:0] registre_4_bits_2_s0_2;

  DEMUX demux_1 (.E(In_0), .SelA(S0_2), .SelB(S1_2), .S0(demux_1_s0), .S1(S0_3));  // open: S2, S3
  DEMUX demux_2 (.E(In_1), .SelA(S1_2), .SelB(S1_2), .S0(demux_2_s0), .S1(S1_3));  // open: S2, S3
  DEMUX demux_3 (.E(In_2), .SelA(S0_2), .SelB(S1_2), .S0(demux_3_s0), .S1(S2_2));  // open: S2, S3
  DEMUX demux_4 (.E(In_3), .SelA(S0_2), .SelB(S1_2), .S0(demux_4_s0), .S1(S3_2));  // open: S2, S3
  Button button_1 (.out(button_1_out));
  or or_1 (or_1_out, S0, demux_1_s0);
  or or_2 (or_2_out, S1, demux_2_s0);
  or or_3 (or_3_out, S2, demux_3_s0);
  or or_4 (or_4_out, S3, demux_4_s0);
  Registre_4_bits registre_4_bits_1 (
    .in_5(button_1_out), .S3(S3_2), .S2(S2_2), .S1(S1_3), .S0(S0_3));  // open: S0_2, S1_2, S2_2, S3_2
  Button button_2 (.out(button_2_out));
  Registre_4_bits registre_4_bits_2 (
    .in_5(button_2_out), .S3(or_4_out), .S2(or_3_out), .S1(or_2_out), .S0(or_1_out),
    .S0_2(registre_4_bits_2_s0_2[0]), .S1_2(registre_4_bits_2_s0_2[1]), .S2_2(registre_4_bits_2_s0_2[2]),
    .S3_2(registre_4_bits_2_s0_2[3]));
  Hex_Digit_Display hex_digit_display_1 (.value(registre_4_bits_2_s0_2));  // open: dp
endmodule

module RS (
  input  R,
  input  S,
  output Q
);

  wire nor_1_out;

  nor nor_1 (nor_1_out, R, Q);
  nor nor_2 (Q, nor_1_out, S);
endmodule

// REG4
module Registre_4_bits (
  input  S3,
  input  S2,
  input  S1,
  input  S0,
  input  in_5,
  output S0_2,
  output S1_2,
  output S2_2,
  output S3_2
);

  RS rs_1 (.R(S0), .S(in_5), .Q(S0_2));
  RS rs_2 (.R(S1), .S(in_5), .Q(S1_2));
  RS rs_3 (.R(S2), .S(in_5), .Q(S2_2));
  RS rs_4 (.R(S3), .S(in_5), .Q(S3_2));
endmodule

module Mux_4 (
  input  selA,
  input  selB,
  input  A,
  input  B,
  input  C,
  input  D,
  output Q
);

  wire and_1_out, and_2_out, and_3_out, and_4_out, not_1_out, not_2_out;

  not not_1 (not_1_out, selA);
  not not_2 (not_2_out, selB);
  and and_1 (and_1_out, A, not_2_out, not_1_out);
  and and_2 (and_2_out, B, not_2_out, selA);
  and and_3 (and_3_out, C, not_1_out, selB);
  and and_4 (and_4_out, D, selB, selA);
  or or_1 (Q, and_1_out, and_2_out, and_3_out, and_4_out);
endmodule

module Full_adder (
  input  A,
  input  B,
  input  Cin,
  output S,
  output Cout
);

  wire and_1_out, and_2_out, xor_1_out;

  xor xor_1 (xor_1_out, A, B);
  xor xor_2 (S, xor_1_out, Cin);
  and and_1 (and_1_out, xor_1_out, Cin);
  and and_2 (and_2_out, A, B);
  or or_1 (Cout, and_1_out, and_2_out);
endmodule

module DEMUX (
  input  SelA,
  input  SelB,
  input  E,
  output S0,
  output S1,
  output S2,
  output S3
);

  wire not_1_out, not_2_out;

  not not_1 (not_1_out, SelB);
  not not_2 (not_2_out, SelA);
  and and_1 (S0, not_2_out, E, not_1_out);
  and and_2 (S1, SelA, E, not_1_out);
  and and_3 (S2, not_2_out, E, SelB);
  and and_4 (S3, SelA, E, SelB);
endmodule

module Alu_1bit (
  input  A,
  input  B,
  input  Cin,
  input  Sel_B,
  input  Sel_A,
  output Cout,
  output S
);

  wire and_1_out, Cin_out, full_adder_1_s, or_1_out;

  and and_1 (and_1_out, B, A);
  or or_1 (or_1_out, B, A);
  Full_adder full_adder_1 (.A(B), .B(A), .Cin(Cin), .S(full_adder_1_s), .Cout(Cout));
  xor u_Cin (Cin_out, B, A);
  Mux_4 mux_4_1 (.selA(Sel_A), .selB(Sel_B), .A(full_adder_1_s), .B(and_1_out), .C(or_1_out), .D(Cin_out), .Q(S));
endmodule

module Alu_4bits (
  input  Sel_B,
  input  Sel_A,
  input  A0,
  input  B0,
  input  Cin,
  input  A1,
  input  B1,
  input  A2,
  input  B2,
  input  A3,
  input  B3,
  output S0,
  output S1,
  output S2,
  output S3,
  output Cout
);

  wire alu_1bit_1_cout, alu_1bit_2_cout, alu_1bit_3_cout;

  Alu_1bit alu_1bit_1 (.Cout(alu_1bit_1_cout), .S(S0), .A(A0), .B(B0), .Cin(Cin), .Sel_B(Sel_B), .Sel_A(Sel_A));
  Alu_1bit alu_1bit_2 (
    .Cout(alu_1bit_2_cout), .S(S1), .A(A1), .B(B1), .Cin(alu_1bit_1_cout), .Sel_B(Sel_B), .Sel_A(Sel_A));
  Alu_1bit alu_1bit_3 (
    .Cout(alu_1bit_3_cout), .S(S2), .A(A2), .B(B2), .Cin(alu_1bit_2_cout), .Sel_B(Sel_B), .Sel_A(Sel_A));
  Alu_1bit alu_1bit_4 (.Cout(Cout), .S(S3), .A(A3), .B(B3), .Cin(alu_1bit_3_cout), .Sel_B(Sel_B), .Sel_A(Sel_A));
endmodule
